# Fritzing sketch abreuvoir_connecte (saved by Fritzing 0.9.3b)

parts:
  Q1 = TIP120 Hi-Current Darlington Transistor
  Q2 = TIP120 Hi-Current Darlington Transistor
  Q3 = TIP120 Hi-Current Darlington Transistor
  Composant1 = Arduino Nano (Rev3.0) (ICSP)
  J5 = Camdenboss CTB0158-2 [part_number=CTB0158-2 package=THT]
  R1 = Resistor [tolerance=±5% resistance=2.2k package="0603 [SMD]"]
  R2 = Resistor [tolerance=±5% resistance=2.2k package="0603 [SMD]"]
  R3 = Resistor [tolerance=±5% resistance=2.2k package="0603 [SMD]"]
  D1 = Rectifier Diode [part_number=1N4001 package="300 mil [THT]"]
  D2 = Rectifier Diode [part_number=1N4001 package="300 mil [THT]"]
  D3 = Rectifier Diode [part_number=1N4001 package="300 mil [THT]"]
  M1 = RioRand LM2596
  VCC1 = Battery block 9V
  J6 = Camdenboss CTB0158-2 [part_number=CTB0158-2 package=THT]
  J7 = Camdenboss CTB0158-2 [part_number=CTB0158-2 package=THT]
  J8 = Infrared Proximity Sensor
  C1 = Capacitor Polarized [package=panasonic_g]
  JP1 = Header 3 [package=molex-1x3_lock]
  J9 = female pin header, 2 pins [form="♀ (female)"]
  JP2 = Header 3 [package=molex-1x3_lock]
  Composant2 = Real Time Clock Module - DS1307 RTC Breakout Board
  Squix1 = OLED 0.96" 128x64 I2C SSD1306

nets:
  N1: Q1.BASE, R1.Pin_0
  N2: Q1.COLLECTOR, J5.pin1, D2.anode
  GND: Q1.EMITTER, Q2.EMITTER, Q3.EMITTER, Composant1.GND, Composant1.A7, M1.Pin_4, J8.Vout, J8.GND, JP1.3, Composant2.GND, Squix1.GND
  N3: Q2.BASE, R3.Pin_0
  N4: Q2.COLLECTOR, D1.anode, J6.pin1
  N5: Q3.BASE, R2.Pin_0
  N6: Q3.COLLECTOR, D3.anode, J7.pin1
  N7: Composant1.D2, JP2.2
  N8: Composant1.D3, JP1.2
  N9: Composant1.D4, R3.Pin_1
  N10: Composant1.D5, R2.Pin_1
  N11: Composant1.D6, R1.Pin_1
  N12: Composant1.D8, J9.pin2
  N13: Composant1.D9, J9.pin1
  VIN: Composant1.VIN, M1.Pin_3, J8.Vcc, JP1.1, JP2.1
  5V: Composant1.5V, Composant2.5V, Squix1.VCC
  N14: Composant1.A5, Composant2.SCL, Squix1.SCL
  N15: Composant1.A4, Composant2.SDA, Squix1.SCA
  N16: J5.pin2, D1.cathode, D2.cathode, D3.cathode, M1.Pin_1, VCC1.+, J6.pin2, J7.pin2, C1.-
  N17: M1.Pin_2, VCC1.-, C1.+

notes:
  Flow sensors
  Pump
  Valve In
  Valve Out
  Presence detector
  RFID reader
